// Logisim project regfile.circ as structural Verilog: 1 circuit, main circuit regfile
module regfile (
  input  [4:0] ReadIndex1,
  input  [4:0] ReadIndex2,
  input  [4:0] WriteIndex,
  input  [31:0] WriteData,
  input  RegWEn,
  input  clk,
  input  [31:0] in_7,
  output [31:0] ra,
  output [31:0] sp,
  output [31:0] t0,
  output [31:0] t1,
  output [31:0] t2,
  output [31:0] s0,
  output [31:0] s1,
  output [31:0] a0,
  output [31:0] ReadData1,
  output [31:0] ReadData2
);

  wire RegWEn0, RegWEn1, RegWEn2, RegWEn3, RegWEn4, RegWEn5, RegWEn6, RegWEn7, RegWEn8, RegWEn9, RegWEn10,
       RegWEn11, RegWEn12, RegWEn13, RegWEn14, RegWEn15, RegWEn16, RegWEn17, RegWEn18, RegWEn19, RegWEn20,
       RegWEn21, RegWEn22, RegWEn23, RegWEn24, RegWEn25, RegWEn26, RegWEn27, RegWEn28, RegWEn29, RegWEn30,
       RegWEn31;
  wire [31:0] inputx1, inputx2, inputx3, inputx4, inputx5, inputx6, inputx7, inputx8, inputx9, inputx10,
       inputx11, inputx12, inputx13, inputx14, inputx15, inputx16, inputx17, inputx18, inputx19, inputx20,
       inputx21, inputx22, inputx23, inputx24, inputx25, inputx26, inputx27, inputx28, inputx29, inputx30,
       inputx31, outputx0, outputx3, outputx4, outputx11, outputx12, outputx13, outputx14, outputx15,
       outputx16, outputx17, outputx18, outputx19, outputx20, outputx21, outputx22, outputx23, outputx24,
       outputx25, outputx26, outputx27, outputx28, outputx29, outputx30, outputx31;

  Register #(.width(32)) x0 (.D(in_7), .en(RegWEn0), .clk(clk), .Q(outputx0));  // open: clr
  Register #(.width(32)) register_1 (.D(inputx8), .en(RegWEn8), .clk(clk), .Q(s0));  // open: clr
  Register #(.width(32)) register_2 (.D(inputx16), .en(RegWEn16), .clk(clk), .Q(outputx16));  // open: clr
  Register #(.width(32)) register_3 (.D(inputx24), .en(RegWEn24), .clk(clk), .Q(outputx24));  // open: clr
  Demultiplexer #(.select(5), .width(32)) demultiplexer_1 (
    .out1(inputx1), .out2(inputx2), .out3(inputx3), .out4(inputx4), .out5(inputx5), .out6(inputx6),
    .out7(inputx7), .out8(inputx8), .out9(inputx9), .out10(inputx10), .out11(inputx11), .out12(inputx12),
    .out13(inputx13), .out14(inputx14), .out15(inputx15), .out16(inputx16), .out17(inputx17),
    .out18(inputx18), .out19(inputx19), .out20(inputx20), .out21(inputx21), .out22(inputx22),
    .out23(inputx23), .out24(inputx24), .out25(inputx25), .out26(inputx26), .out27(inputx27),
    .out28(inputx28), .out29(inputx29), .out30(inputx30), .out31(inputx31), .in(WriteData), .sel(WriteIndex));  // open: out0
  Demultiplexer #(.select(5)) demultiplexer_2 (
    .out0(RegWEn0), .out1(RegWEn1), .out2(RegWEn2), .out3(RegWEn3), .out4(RegWEn4), .out5(RegWEn5),
    .out6(RegWEn6), .out7(RegWEn7), .out8(RegWEn8), .out9(RegWEn9), .out10(RegWEn10), .out11(RegWEn11),
    .out12(RegWEn12), .out13(RegWEn13), .out14(RegWEn14), .out15(RegWEn15), .out16(RegWEn16),
    .out17(RegWEn17), .out18(RegWEn18), .out19(RegWEn19), .out20(RegWEn20), .out21(RegWEn21),
    .out22(RegWEn22), .out23(RegWEn23), .out24(RegWEn24), .out25(RegWEn25), .out26(RegWEn26),
    .out27(RegWEn27), .out28(RegWEn28), .out29(RegWEn29), .out30(RegWEn30), .out31(RegWEn31), .in(RegWEn),
    .sel(WriteIndex));
  Register #(.width(32)) register_4 (.D(inputx1), .en(RegWEn1), .clk(clk), .Q(ra));  // open: clr
  Register #(.width(32)) register_5 (.D(inputx9), .en(RegWEn9), .clk(clk), .Q(s1));  // open: clr
  Register #(.width(32)) register_6 (.D(inputx17), .en(RegWEn17), .clk(clk), .Q(outputx17));  // open: clr
  Register #(.width(32)) register_7 (.D(inputx25), .en(RegWEn25), .clk(clk), .Q(outputx25));  // open: clr
  Multiplexer #(.select(5), .width(32)) multiplexer_1 (
    .in0(outputx0), .in1(ra), .in2(sp), .in3(outputx3), .in4(outputx4), .in5(t0), .in6(t1), .in7(t2),
    .in8(s0), .in9(s1), .in10(a0), .in11(outputx11), .in12(outputx12), .in13(outputx13), .in14(outputx14),
    .in15(outputx15), .in16(outputx16), .in17(outputx17), .in18(outputx18), .in19(outputx19),
    .in20(outputx20), .in21(outputx21), .in22(outputx22), .in23(outputx23), .in24(outputx24),
    .in25(outputx25), .in26(outputx26), .in27(outputx27), .in28(outputx28), .in29(outputx29),
    .in30(outputx30), .in31(outputx31), .out(ReadData1), .sel(ReadIndex1));
  Register #(.width(32)) register_8 (.D(inputx2), .en(RegWEn2), .clk(clk), .Q(sp));  // open: clr
  Register #(.width(32)) register_9 (.D(inputx10), .en(RegWEn10), .clk(clk), .Q(a0));  // open: clr
  Register #(.width(32)) register_10 (.D(inputx18), .en(RegWEn18), .clk(clk), .Q(outputx18));  // open: clr
  Register #(.width(32)) register_11 (.D(inputx26), .en(RegWEn26), .clk(clk), .Q(outputx26));  // open: clr
  Multiplexer #(.select(5), .width(32)) multiplexer_2 (
    .in0(outputx0), .in1(ra), .in2(sp), .in3(outputx3), .in4(outputx4), .in5(t0), .in6(t1), .in7(t2),
    .in8(s0), .in9(s1), .in10(a0), .in11(outputx11), .in12(outputx12), .in13(outputx13), .in14(outputx14),
    .in15(outputx15), .in16(outputx16), .in17(outputx17), .in18(outputx18), .in19(outputx19),
    .in20(outputx20), .in21(outputx21), .in22(outputx22), .in23(outputx23), .in24(outputx24),
    .in25(outputx25), .in26(outputx26), .in27(outputx27), .in28(outputx28), .in29(outputx29),
    .in30(outputx30), .in31(outputx31), .out(ReadData2), .sel(ReadIndex2));
  Register #(.width(32)) register_12 (.D(inputx3), .en(RegWEn3), .clk(clk), .Q(outputx3));  // open: clr
  Register #(.width(32)) register_13 (.D(inputx11), .en(RegWEn11), .clk(clk), .Q(outputx11));  // open: clr
  Register #(.width(32)) register_14 (.D(inputx19), .en(RegWEn19), .clk(clk), .Q(outputx19));  // open: clr
  Register #(.width(32)) register_15 (.D(inputx27), .en(RegWEn27), .clk(clk), .Q(outputx27));  // open: clr
  Register #(.width(32)) register_16 (.D(inputx4), .en(RegWEn4), .clk(clk), .Q(outputx4));  // open: clr
  Register #(.width(32)) register_17 (.D(inputx12), .en(RegWEn12), .clk(clk), .Q(outputx12));  // open: clr
  Register #(.width(32)) register_18 (.D(inputx20), .en(RegWEn20), .clk(clk), .Q(outputx20));  // open: clr
  Register #(.width(32)) register_19 (.D(inputx28), .en(RegWEn28), .clk(clk), .Q(outputx28));  // open: clr
  Register #(.width(32)) register_20 (.D(inputx5), .en(RegWEn5), .clk(clk), .Q(t0));  // open: clr
  Register #(.width(32)) register_21 (.D(inputx13), .en(RegWEn13), .clk(clk), .Q(outputx13));  // open: clr
  Register #(.width(32)) register_22 (.D(inputx21), .en(RegWEn21), .clk(clk), .Q(outputx21));  // open: clr
  Register #(.width(32)) register_23 (.D(inputx29), .en(RegWEn29), .clk(clk), .Q(outputx29));  // open: clr
  Register #(.width(32)) register_24 (.D(inputx6), .en(RegWEn6), .clk(clk), .Q(t1));  // open: clr
  Register #(.width(32)) register_25 (.D(inputx14), .en(RegWEn14), .clk(clk), .Q(outputx14));  // open: clr
  Register #(.width(32)) register_26 (.D(inputx22), .en(RegWEn22), .clk(clk), .Q(outputx22));  // open: clr
  Register #(.width(32)) register_27 (.D(inputx30), .en(RegWEn30), .clk(clk), .Q(outputx30));  // open: clr
  Register #(.width(32)) register_28 (.D(inputx7), .en(RegWEn7), .clk(clk), .Q(t2));  // open: clr
  Register #(.width(32)) register_29 (.D(inputx15), .en(RegWEn15), .clk(clk), .Q(outputx15));  // open: clr
  Register #(.width(32)) register_30 (.D(inputx23), .en(RegWEn23), .clk(clk), .Q(outputx23));  // open: clr
  Register #(.width(32)) register_31 (.D(inputx31), .en(RegWEn31), .clk(clk), .Q(outputx31));  // open: clr

  // Other names for the same wires on the sheet: outputx1[31:0] = ra; outputx2[31:0] = sp; outputx5[31:0] = t0;
  //   outputx6[31:0] = t1; outputx7[31:0] = t2; outputx8[31:0] = s0; outputx9[31:0] = s1; outputx10[31:0] = a0

  // Notes on the sheet:
  //   INPUTS to your circuit
  //   DON'T CHANGE THE LOCATIONS OF THE INPUTS AND OUTPUTS!
  //   These are DEBUG/TEST outputs from your circuit.
  //   OUTPUTS from your circuit
endmodule
